# Fritzing sketch TestMCP3008 (saved by Fritzing 0.9.3b)
circuit board: 8.46667cm x 5.64444cm
breadboards: 1

parts:
  IC1 = MCP3008 8-channel 10-bit ADC [part_number=MCP3008]
  Raspberry_Pi_1 = Raspberry Pi B rev2
  CNY2 = CNY70
  R1 = Resistor [tolerance=±5% resistance=180 package=THT]
  R2 = Resistor [tolerance=±5% resistance=10k package=THT]

nets:
  N1: IC1.no_name_yet#1, CNY2.Emisor, CNY2.Catodo, R1.Pin_1, R2.Pin_1
  N2: IC1.no_name_yet#9, IC1.no_name_yet#14, Raspberry_Pi_1.GND, R1.Pin_0, R2.Pin_0
  N3: IC1.no_name_yet#10, Raspberry_Pi_1.GPIO_25
  N4: IC1.no_name_yet#11, Raspberry_Pi_1.GPIO_24
  N5: IC1.no_name_yet#12, Raspberry_Pi_1.GPIO_23
  N6: IC1.no_name_yet#13, Raspberry_Pi_1.GPIO_18
  N7: IC1.no_name_yet#15, IC1.no_name_yet#16, Raspberry_Pi_1.3V3
  N8: Raspberry_Pi_1.5V, CNY2.Colector, CNY2.Anodo

custom parts:
  CNY70: Sensor de Infrarojos de corto alcance.

// code stored in the sketch: TestMCP3008.ino

