# Fritzing sketch Untitled Sketch 2 (saved by Fritzing 0.9.3b)
breadboards: 1

parts:
  IC1 = MCP3008 8-channel 10-bit ADC [part_number=MCP3008]
  Raspberry_Pi_1 = Raspberry Pi B rev2
  U1 = POT [package=trim_pot]

nets:
  N1: IC1.no_name_yet#1, U1.E
  N2: IC1.no_name_yet#10, Raspberry_Pi_1.GPIO_25
  N3: IC1.no_name_yet#11, Raspberry_Pi_1.GPIO_24
  N4: IC1.no_name_yet#12, Raspberry_Pi_1.GPIO_23
  N5: IC1.no_name_yet#13, Raspberry_Pi_1.GPIO_18
  N6: IC1.no_name_yet#14, Raspberry_Pi_1.GND, U1.A
  N7: IC1.no_name_yet#15, IC1.no_name_yet#16, Raspberry_Pi_1.3V3, U1.S
