# Fritzing sketch esp8266 (saved by Fritzing 0.9.3b)
breadboards: 1

parts:
  U1 = ESP8266 WiFi Module [part_number=ESP8266]
  Part1 = FTDI Basic Programmer
  Part2 = Arduino Uno (Rev3)

nets:
  N1: U1.RXD, Part1.TXO
  VCC: U1.VCC, U1.CH_PD, Part1.POWER, Part2.3V3
  GND: U1.GND, Part1.GND, Part2.GND
  N2: U1.TXD, Part1.RXI
