# Fritzing sketch TestMCP3008 (saved by Fritzing 0.9.3b)
circuit board: 8.46667cm x 5.64444cm
breadboards: 1

parts:
  IC1 = MCP3008 8-channel 10-bit ADC [part_number=MCP3008]
  Raspberry_Pi_1 = Raspberry Pi B rev2
  CNY2 = CNY70
  R1 = Resistor [tolerance=±5% resistance=180 package=THT]
  R2 = Resistor [tolerance=±5% resistance=10k package=THT]
  LED1 = LED - 5mm [color="Yellow (595nm)" package="5 mm [THT]"]
  LED2 = LED - 5mm [color="Yellow (595nm)" package="5 mm [THT]"]
  LED3 = LED - 5mm [color="Yellow (595nm)" package="5 mm [THT]"]
  R3 = Resistor [tolerance=±5% resistance=220 package=THT]
  R4 = Resistor [tolerance=±5% resistance=220 package=THT]
  R5 = Resistor [tolerance=±5% resistance=220 package=THT]
  R6 = Resistor [tolerance=±5% resistance=180 package=THT]
  R7 = Resistor [tolerance=±5% resistance=10k package=THT]
  R8 = Resistor [tolerance=±5% resistance=180 package=THT]
  R9 = Resistor [tolerance=±5% resistance=10k package=THT]
  CNY3 = CNY70
  CNY4 = CNY70
  M1 = Stepper Motor - Unipolar
  M2 = Stepper Motor - Unipolar
  IC2 = SHIFT REGISTER [package=dil16]  # not connected
  U1 = LCD-16X2 [package=lcd-8x2]  # not connected

nets:
  N1: IC1.no_name_yet#1, CNY2.Emisor, CNY2.Catodo, R1.Pin_1, R2.Pin_1
  N2: IC1.no_name_yet#2, R7.Pin_1, CNY3.Emisor
  N3: IC1.no_name_yet#3, R9.Pin_1, CNY4.Emisor
  N4: IC1.no_name_yet#9, IC1.no_name_yet#14, Raspberry_Pi_1.GND, R1.Pin_0, R2.Pin_0, LED1.anode, LED3.anode, R6.Pin_0, R7.Pin_0, R8.Pin_0, R9.Pin_0, M1.D, M2.D
  N5: IC1.no_name_yet#10, Raspberry_Pi_1.GPIO_25
  N6: IC1.no_name_yet#11, Raspberry_Pi_1.GPIO_24
  N7: IC1.no_name_yet#12, Raspberry_Pi_1.GPIO_23
  N8: IC1.no_name_yet#13, Raspberry_Pi_1.GPIO_18
  N9: IC1.no_name_yet#15, IC1.no_name_yet#16, Raspberry_Pi_1.3V3
  N10: Raspberry_Pi_1.5V, CNY2.Colector, CNY2.Anodo, CNY3.Colector, CNY3.Anodo, CNY4.Colector, CNY4.Anodo, M1.A, M2.A
  N11: Raspberry_Pi_1.GPIO_2, M2.COMMON_2
  N12: Raspberry_Pi_1.GPIO_3, M2.B
  N13: Raspberry_Pi_1.GPIO_17, M2.COMMON_1
  N14: Raspberry_Pi_1.GPIO_27, M1.COMMON_2
  N15: Raspberry_Pi_1.GPIO_22, M1.B
  N16: Raspberry_Pi_1.GPIO_4, M2.C
  N17: Raspberry_Pi_1.GPIO_10, M1.C
  N18: Raspberry_Pi_1.GPIO_9, M1.COMMON_1
  N19: Raspberry_Pi_1.GPIO_11, R4.Pin_1
  N20: Raspberry_Pi_1.GPIO_8, R5.Pin_1
  N21: Raspberry_Pi_1.GPIO_7, R3.Pin_1
  N22: LED1.cathode, R3.Pin_0
  N23: LED2.cathode, R4.Pin_0
  N24: LED3.cathode, R5.Pin_0
  N25: R6.Pin_1, CNY3.Catodo
  N26: R8.Pin_1, CNY4.Catodo

custom parts:
  CNY70: Sensor de Infrarojos de corto alcance.

// code stored in the sketch: TestMCP3008.ino

