# Fritzing sketch drivebot (saved by Fritzing 0.9.3b)
breadboards: 1

parts:
  Part1 = Arduino Uno (Rev3)
  S1 = Pushbutton [package="[THT]"]
  IC1 = MCP3008 8-channel 10-bit ADC [part_number=MCP3008]  # not connected
  IC2 = SHIFT REGISTER [package=dil16]
  R1 = Resistor [tolerance=±5% resistance=180 package=THT]
  R2 = Resistor [tolerance=±5% resistance=10k package=THT]
  R3 = Resistor [tolerance=±5% resistance=180 package=THT]
  R4 = Resistor [tolerance=±5% resistance=10k package=THT]
  R5 = Resistor [tolerance=±5% resistance=180 package=THT]
  R6 = Resistor [tolerance=±5% resistance=10k package=THT]
  CNY2 = CNY70
  CNY3 = CNY70
  CNY4 = CNY70
  LED1 = LED - 3mm [color="Orange (605nm)" package="3 mm [THT]"]
  LED2 = LED - 3mm [color="Orange (605nm)" package="3 mm [THT]"]
  LED3 = LED - 3mm [color="Orange (605nm)" package="3 mm [THT]"]
  R7 = Resistor [tolerance=±5% resistance=180 package=THT]
  R8 = Resistor [tolerance=±5% resistance=180 package=THT]
  R9 = Resistor [tolerance=±5% resistance=180 package=THT]
  R10 = Resistor [tolerance=±5% resistance=220 package=THT]
  M1 = Stepper Motor - Bipolar
  M2 = Stepper Motor - Bipolar
  LCD1 = LCD screen
  R11 = Trimmer Potentiometer [maximum_resistance=10kΩ package=THT]

nets:
  N1: Part1.A0, R2.Pin_0, CNY4.Emitter
  N2: Part1.A1, R4.Pin_0, CNY3.Emitter
  N3: Part1.A2, R6.Pin_0, CNY2.Emitter
  N4: Part1.D8, IC2.RCK
  N5: Part1.D9_PWM, IC2.SER
  N6: Part1.D10_PWM/SS, S1.Pin_1, S1.Pin_2, R10.Pin_0
  N7: Part1.D11_PWM/MOSI, R9.Pin_1
  N8: Part1.D12/MISO, R8.Pin_1
  N9: Part1.D13/SCK, R7.Pin_1
  N10: Part1.D1/TX, LCD1.DB7
  N11: Part1.D2, LCD1.DB6
  N12: Part1.D3_PWM, LCD1.DB5
  N13: Part1.D4, LCD1.DB4
  N14: Part1.D5_PWM, LCD1.E
  N15: Part1.D6_PWM, LCD1.RS
  N16: Part1.D7, IC2.SCK
  VCC: S1.Pin_3, S1.Pin_4, IC2.SCL, IC2.VCC, R1.Pin_1, R2.Pin_1, R3.Pin_1, R4.Pin_1, R5.Pin_1, R6.Pin_1, LED1.cathode, LED2.cathode, LED3.cathode, LCD1.VSS, LCD1.R/W, LCD1.LED-, R11.leg2
  N17: IC2.QB, M1.B
  N18: IC2.QC, M1.C
  N19: IC2.QD, M1.A
  N20: IC2.QE, M2.D
  N21: IC2.QF, M2.B
  N22: IC2.QG, M2.C
  N23: IC2.QH, M2.A
  N24: IC2.G, CNY2.Colector, CNY2.Anode, CNY3.Colector, CNY3.Anode, CNY4.Colector, CNY4.Anode, R10.Pin_1, LCD1.VDD, LCD1.LED+, R11.leg1
  N25: IC2.QA, M1.D
  N26: R1.Pin_0, CNY4.Cathode
  N27: R3.Pin_0, CNY3.Cathode
  N28: R5.Pin_0, CNY2.Cathode
  N29: LED1.anode, R7.Pin_0
  N30: LED2.anode, R8.Pin_0
  N31: LED3.anode, R9.Pin_0
  N32: LCD1.V0, R11.wiper
